# Fritzing sketch thermocontrol (saved by Fritzing 0.9.0b)
breadboards: 1

parts:
  Composant1 = Arduino Uno (Rev3)
  R1 = Resistor [tolerance=±5% resistance=1k package=THT]
  T2 = LM35 Temperature Sensor [package="TO92 [THT]"]
  S1 = Pushbutton [package="[THT]"]
  S2 = Pushbutton [package="[THT]"]
  S3 = Pushbutton [package="[THT]"]
  R2 = Trimmer Potentiometer [maximum_resistance=100kΩ package=THT]
  D1 = Rectifier Diode [part_number=1N4001 breakdown_voltage=3.6V package="300 mil [THT]"]
  C1 = Ceramic Capacitor [capacitance=10nF voltage=6.3V package="100 mil [THT, multilayer]"]
  LED1 = LED - 5mm [color="Red (633nm)" package="5 mm [THT]"]
  R3 = Resistor [tolerance=±5% resistance=1k package=THT]
  R4 = Resistor [tolerance=±5% resistance=220 package=THT]
  Q1 = NPN-Transistor [part_number=BC547 package="TO92 [THT]"]
  M1 = DC Motor [part_number=Fan]
  T3 = LM35 Temperature Sensor [package="TO92 [THT]"]
  LCD1 = LCD screen

nets:
  N1: Composant1.A0, T3.Vout
  N2: Composant1.A1, T2.Vout
  N3: Composant1.D8, LCD1.RS
  N4: Composant1.D10_PWM/SS, S1.Pin_3, S1.Pin_4
  N5: Composant1.D11_PWM/MOSI, S2.Pin_3, S2.Pin_4
  N6: Composant1.D12/MISO, S3.Pin_3, S3.Pin_4
  N7: Composant1.D13/SCK, LED1.cathode, R4.Pin_1
  GND: Composant1.GND, S1.Pin_1, S1.Pin_2, S2.Pin_1, S2.Pin_2, S3.Pin_1, S3.Pin_2, R2.leg1, R3.Pin_0, Q1.C, T3.GND
  N8: Composant1.D2, R1.Pin_1
  N9: Composant1.D3_PWM, LCD1.DB7
  N10: Composant1.D4, LCD1.DB6
  N11: Composant1.D5_PWM, LCD1.DB5
  N12: Composant1.D6_PWM, LCD1.DB4
  N13: Composant1.D7, LCD1.E
  N14: Composant1.5V, R2.leg2, T3.+Vs
  N15: Composant1.VIN, D1.cathode, C1.0, M1.pin_2
  N16: R1.Pin_0, LCD1.LED+
  N17: T2.+Vs, LCD1.VDD
  GND_2: T2.GND, LCD1.VSS, LCD1.R/W, LCD1.LED-
  N18: R2.wiper, LCD1.V0
  N19: D1.anode, C1.1, Q1.E, M1.pin_1
  N20: LED1.anode, R3.Pin_1
  N21: R4.Pin_0, Q1.B
